# Fritzing sketch Breadboard Prototype (saved by Fritzing 0.9.4)
breadboards: 1

parts:
  Part1 = Arduino Uno (Rev3)
  R1 = Resistor [tolerance=±5% resistance=220 package=THT]
  LED1 = LED - 5mm [color="Red (633nm)" package="5 mm [THT]"]
  S1 = Pushbutton [package="[THT]"]
  R2 = Resistor [tolerance=±5% resistance=10k package=THT]
  R3 = Rotary Potentiometer (Large) [maximum_resistance=100kΩ package=THT]

nets:
  N1: Part1.A0, R3.wiper
  N2: Part1.D9_PWM, R1.Pin_1
  N3: Part1.D2, S1.Pin_3, S1.Pin_4, R2.Pin_0
  N4: Part1.5V, R2.Pin_1, R3.leg2
  N5: Part1.GND, LED1.cathode, S1.Pin_1, S1.Pin_2, R3.leg1
  N6: R1.Pin_0, LED1.anode
